// Logisim project ex1.circ as structural Verilog: 5 circuits, main circuit NAND1
module NAND1 (
  input  A,
  input  B,
  output RESULT
);

  wire and_1_out;

  and and_1 (and_1_out, A, B);
  not not_1 (RESULT, and_1_out);

  // Notes on the sheet:
  //   PUT CIRCUITRY HERE
endmodule

module NOR1 (
  input  A,
  input  B,
  output RESULT
);

  wire or_1_out;

  or or_1 (or_1_out, A, B);
  not not_1 (RESULT, or_1_out);

  // Notes on the sheet:
  //   PUT CIRCUITRY HERE
endmodule

module XOR1 (
  input  A,
  input  B,
  output RESULT
);

  wire and_1_out, and_2_out, not_1_out, not_2_out;

  not not_1 (not_1_out, A);
  and and_1 (and_1_out, A, not_2_out);
  not not_2 (not_2_out, B);
  and and_2 (and_2_out, not_1_out, B);
  or or_1 (RESULT, and_1_out, and_2_out);

  // Notes on the sheet:
  //   PUT CIRCUITRY HERE
endmodule

module MUX2 (
  input  A,
  input  B,
  input  Sel,
  output RESULT
);

  wire and_1_out, and_2_out, and_3_out, and_4_out, and_5_out, and_6_out, and_7_out, and_8_out, not_1_out,
       not_2_out, not_3_out, not_4_out, or_1_out, or_2_out;

  not not_1 (not_1_out, A);
  not not_2 (not_2_out, B);
  and and_1 (and_1_out, A, B);
  and and_2 (and_2_out, not_1_out, B);
  and and_3 (and_3_out, A, B);
  not not_3 (not_3_out, Sel);
  and and_4 (and_4_out, A, not_2_out);
  not not_4 (not_4_out, Sel);
  and and_5 (and_5_out, and_1_out, Sel);
  and and_6 (and_6_out, and_2_out, Sel);
  and and_7 (and_7_out, and_3_out, not_3_out);
  and and_8 (and_8_out, and_4_out, not_4_out);
  or or_1 (or_1_out, and_5_out, and_6_out);
  or or_2 (or_2_out, and_7_out, and_8_out);
  or or_3 (RESULT, or_1_out, or_2_out);

  // Notes on the sheet:
  //   PUT CIRCUITRY HERE
endmodule

module MUX4 (
  input  A,
  input  B,
  input  C,
  input  D,
  input  Sel1,
  input  Sel2,
  output RESULT
);

  wire mux2_1_result, mux2_2_result;

  MUX2 mux2_1 (.A(A), .B(B), .Sel(Sel1), .RESULT(mux2_1_result));
  MUX2 mux2_2 (.A(C), .B(D), .Sel(Sel1), .RESULT(mux2_2_result));
  MUX2 mux2_3 (.A(mux2_1_result), .B(mux2_2_result), .Sel(Sel2), .RESULT(RESULT));

  // Notes on the sheet:
  //   PUT CIRCUITRY HERE
endmodule
